# Fritzing sketch 1 (saved by Fritzing 0.9.4)
breadboards: 1

parts:
  R2 = Resistor [tolerance=±5% resistance=220 package=THT]
  LED = LED - 5mm [color="Red (633nm)" package="5 mm [THT]"]
  U1 = NodeMCU V1.0

nets:
  N1: R2.Pin_0, LED.cathode
  N2: R2.Pin_1, U1.GND#6
  N3: LED.anode, U1.D0

custom parts:
  NodeMCU V1.0: ESP8266 based NodeMCU V1.0

// code stored in the sketch: 1.fzz.ino
const int led=16;


void setup() {
  pinMode(led, OUTPUT);
}


void loop() {
  digitalWrite(led, HIGH);
  delay(1000);
  digitalWrite(led, LOW);
  delay(1000);                 
}
