# Fritzing sketch 3 (saved by Fritzing 0.9.4)
breadboards: 1

parts:
  U1 = NodeMCU V1.0
  R1 = Resistor [tolerance=±5% resistance=220 package=THT]
  LED1 = LED - 5mm [color="Red (633nm)" package="5 mm [THT]"]

nets:
  N1: U1.GND#6, R1.Pin_0
  N2: U1.D5, LED1.anode
  N3: R1.Pin_1, LED1.cathode

custom parts:
  NodeMCU V1.0: ESP8266 based NodeMCU V1.0

// code stored in the sketch: 3.fzz.ino
const int led = 14;


void setup() {
  Serial.begin(115200);
  pinMode(led, OUTPUT);
}


void loop() {
  for(int i=0; i<255; i++) {
    analogWrite(led,i);
    Serial.println(i);
    delay(10);
  }
}
