# Fritzing sketch 4 (saved by Fritzing 0.9.4)
breadboards: 1

parts:
  U1 = NodeMCU V1.0
  R1 = Resistor [tolerance=±5% resistance=220 package=THT]
  LED1 = LED - 5mm [color="Red (633nm)" package="5 mm [THT]"]
  U3 = POT [package=pot_mammoth]

nets:
  N1: U1.3V3#5, U3.S
  N2: U1.GND#6, R1.Pin_0, U3.E
  N3: U1.D5, LED1.anode
  N4: U1.A0, U3.A
  N5: R1.Pin_1, LED1.cathode

custom parts:
  NodeMCU V1.0: ESP8266 based NodeMCU V1.0

// code stored in the sketch: 4.fzz.ino
#define led D5
#define pot A0

void setup(){
  Serial.begin(115200);
  pinMode(led,OUTPUT);
  pinMode(pot,INPUT);
}

void loop(){
  int potenciometro=analogRead(pot); 
  Serial.println(potenciometro);
  analogWrite(led,potenciometro);
}
