# Fritzing sketch 5 (saved by Fritzing 0.9.4)
breadboards: 1

parts:
  U2 = NodeMCU V1.0
  R1 = Photocell (LDR) [package=THT]
  R2 = Resistor [tolerance=±5% resistance=10k package="2010 [SMD]"]
  LED1 = LED - 3mm [color="Red (633nm)" package="3 mm [THT]"]
  R3 = Resistor [tolerance=±5% resistance=220 package=THT]

nets:
  N1: U2.3V3#5, R2.Pin_1
  N2: U2.GND#6, R3.Pin_1
  N3: U2.D5, LED1.anode
  N4: U2.A0, R1.pin_0
  N5: R1.pin_1, R2.Pin_0
  N6: LED1.cathode, R3.Pin_0

custom parts:
  NodeMCU V1.0: ESP8266 based NodeMCU V1.0

// code stored in the sketch: 5.fzz.ino
#define led D5
#define ldr A0


void setup(){
  Serial.begin(115200);
  pinMode(led,OUTPUT);
  pinMode(ldr,INPUT);
}


void loop(){
  int luminosidade=analogRead(ldr); 
  Serial.println(luminosidade);
  delay(10);
  if(luminosidade>400){
    digitalWrite(led,HIGH);
  }
  else {
    digitalWrite(led,LOW);
  }
}
