# Fritzing sketch 2 (saved by Fritzing 0.9.4)
breadboards: 1

parts:
  R1 = Resistor [tolerance=±5% resistance=10k package=THT]
  R2 = Resistor [tolerance=±5% resistance=220 package=THT]
  LED = LED - 5mm [color="Red (633nm)" package="5 mm [THT]"]
  Push_Button = Momentary Switch [package=ksa_sealed_tac_switch]
  U1 = NodeMCU V1.0

nets:
  N1: R1.Pin_0, Push_Button.2, U1.D8
  N2: R1.Pin_1, U1.GND#13
  N3: R2.Pin_0, LED.cathode
  N4: R2.Pin_1, U1.GND#6
  N5: LED.anode, U1.D0
  N6: Push_Button.4, U1.3V3#14

custom parts:
  NodeMCU V1.0: ESP8266 based NodeMCU V1.0

// code stored in the sketch: 2.fzz.ino
const int pushButton = D8;
const int led        = D0;


void setup() {
  Serial.begin(115200);
  pinMode(pushButton, INPUT);
  pinMode(led, OUTPUT);
}


void loop() {
  int buttonState = digitalRead(pushButton);
  Serial.println(buttonState);
  digitalWrite(led,buttonState);
  delay(1);
}
