# Fritzing sketch I2C2 (saved by Fritzing 0.9.4)
circuit board: 8.46667cm x 5.64444cm
breadboards: 1

parts:
  LCM1602_IIC1 = LCM1602 IIC [part_number="LCM1602 IIC" chip_label="LCM1602 IIC" package="DIP (Dual Inline) [THT]"]
  U1 = NodeMCU V1.0
  LCD2 = 20x4 LCD display [part_number=2004A]

nets (from the breadboard view):
  VSS: LCM1602_IIC1.VSS, LCD2.Vss
  VDD: LCM1602_IIC1.VDD, LCD2.Vdd
  N1: LCM1602_IIC1.V0, LCD2.Vo
  N2: LCM1602_IIC1.RS, LCD2.RS
  N3: LCM1602_IIC1.RW, LCD2.R/W
  N4: LCM1602_IIC1.E, LCD2.E
  N5: LCM1602_IIC1.D0, LCD2.DB0
  N6: LCM1602_IIC1.D1, LCD2.DB1
  N7: LCM1602_IIC1.D2, LCD2.DB2
  N8: LCM1602_IIC1.D3, LCD2.DB3
  N9: LCM1602_IIC1.D4, LCD2.DB4
  N10: LCM1602_IIC1.D5, LCD2.DB5
  N11: LCM1602_IIC1.D6, LCD2.DB6
  N12: LCM1602_IIC1.D7, LCD2.DB7
  N13: LCM1602_IIC1.A, LCD2.A_+
  N14: LCM1602_IIC1.K, LCD2.K_-
  GND: LCM1602_IIC1.GND, U1.GND
  VCC: LCM1602_IIC1.VCC, LCM1602_IIC1.LED_A, U1.Vin
  N15: LCM1602_IIC1.SDA, LCM1602_IIC1.LED_B, U1.D2
  N16: LCM1602_IIC1.SCL, U1.D1

custom parts:
  LCM1602 IIC: I2C-Module to use a 1602 or 2004 LCD on with the wire.h libory Serial LCD Modul
  NodeMCU V1.0: ESP8266 based NodeMCU V1.0
  20x4 LCD display: 20x4 character display. CHECK LED POLARITY BEFORE CONNECTING POWER Some versions of the dispaly have the polarity of the LED pins "A" and "K" reversed.

// code stored in the sketch: AnalogReadSerial2LCD_LED.ino
#include <Wire.h>
#include <LiquidCrystal_I2C.h>

LiquidCrystal_I2C lcd(0x27,20,4);

void setup()
{
 lcd.init();
}
 
void loop()
{
  lcd.setBacklight(HIGH);
  lcd.setCursor(0,0);
  lcd.print("PET Eletrica");
  lcd.setCursor(0,1);
  lcd.print("LCD e modulo I2C");
  delay(1000);
  lcd.setBacklight(LOW);
  delay(1000);
}
