# Fritzing sketch circuito-digital (saved by Fritzing 0.8.7b)
breadboards: 1

parts:
  U1 = NodeMCU V1.0
  부품3 = FC-28 Soil Hygrometer Module - Probe
  부품4 = FC-28 Soil Hygrometer Module

nets:
  N1: U1.D5, 부품4.DO
  N2: U1.GND#13, 부품4.GND
  N3: U1.3V3#14, 부품4.VCC
  N4: 부품3.POS, 부품4.POS
  N5: 부품3.NEG, 부품4.NEG

custom parts:
  NodeMCU V1.0: ESP8266 based NodeMCU V1.0
  FC-28 Soil Hygrometer Module - Probe: The FC-28 is a soil hygrometer module that uses the Texas Instruments LM393 comparator chip to provide an analog measurement of soil humidity.
  FC-28 Soil Hygrometer Module: The FC-28 is a soil hygrometer module that uses the Texas Instruments LM393 comparator chip to provide an analog measurement of soil humidity. The digital output is high when soil moisture is over a certain threshold, as determined by adjusting the potentiometer.

// code stored in the sketch: 3.fzz.ino
const int led = 14;


void setup() {
  Serial.begin(115200);
  pinMode(led, OUTPUT);
}


void loop() {
  for(int i=0; i<255; i++) {
    analogWrite(led,i);
    Serial.println(i);
    delay(10);
  }
}
