# Fritzing sketch circuito (saved by Fritzing 0.9.4)
breadboards: 1

parts:
  U1 = NodeMCU V1.0
  LED2 = smd LED [color="Red (633nm)" package="0603 [SMD]"]
  LED3 = smd LED [color="Green (555nm)" package="0603 [SMD]"]
  LED4 = smd LED [color="Blue (430nm)" package="0603 [SMD]"]
  LED1 = smd LED [color="Yellow (595nm)" package="0603 [SMD]"]
  R1 = Resistor [tolerance=±5% resistance=220 package="0402 [SMD]"]
  R2 = Resistor [tolerance=±5% resistance=220 package="0402 [SMD]"]
  R3 = Resistor [tolerance=±5% resistance=220 package="0402 [SMD]"]
  R5 = Resistor [tolerance=±5% resistance=220 package="0402 [SMD]"]

nets:
  N1: U1.D0, LED1.anode
  N2: U1.D1, U1.GND, U1.D5, U1.D6, U1.D7, U1.D8, U1.RX, U1.TX, LED4.anode, R1.Pin_0, R2.Pin_0, R3.Pin_0, R5.Pin_0
  N3: U1.D2, LED2.anode
  N4: U1.D4, LED3.anode
  N5: LED2.cathode, R2.Pin_1
  N6: LED3.cathode, R3.Pin_1
  N7: LED4.cathode, R5.Pin_1
  N8: LED1.cathode, R1.Pin_1

custom parts:
  NodeMCU V1.0: ESP8266 based NodeMCU V1.0
